# Fritzing sketch I2C_MasterSlaveTest (saved by Fritzing 0.9.3b)
breadboards: 1

parts:
  パーツ1 = Arduino Uno (Rev3) - ICSP
  W1 = ESPr Developer [package="DIP (Dual Inline) [THT]"]

nets:
  N1: パーツ1.A4/SDA, W1.IO4
  N2: パーツ1.A5/SCL, W1.IO5
  N3: パーツ1.GND, W1.GND#20
