# Fritzing sketch ServoTest (saved by Fritzing 0.9.3b)
breadboards: 1

parts:
  パーツ1 = Arduino Uno (Rev3) - ICSP
  J1 = Basic Servo
  POT1 = Breadboard Trimpot  # not connected

nets:
  N1: パーツ1.D5_PWM, J1.pulse
  5V: パーツ1.5V, J1.vcc
  GND: パーツ1.GND, J1.gnd
