# Fritzing sketch RCCar_Sketch (saved by Fritzing 0.9.3b)
breadboards: 2

parts:
  パーツ1 = Arduino Pro Mini (5V)
  M1 = DC Motor
  M2 = DC Motor
  M3 = DC Motor
  M4 = DC Motor
  J1 = Basic Servo
  J2 = Basic Servo
  BAT1 = Battery Holders [package=battery-aa-kit]
  BAT2 = Battery Holders [package=battery-aa-kit]
  BAT4 = Battery Holders [package=battery-aa-kit]
  BAT5 = Battery Holders [package=battery-aa-kit]
  W2 = ESPr Developer [package="DIP (Dual Inline) [THT]"]
  U1 = Voltage Regulator - 5V [package="DPak [SMD]"]
  VCC1 = 4 x AAA Battery Mount
  BAT3 = Battery Holders [package=battery-aa-kit]
  パーツ4 = DRV8838
  パーツ5 = DRV8838
  パーツ6 = DRV8838
  パーツ7 = DRV8838

nets:
  N1: パーツ1.A4, W2.IO4
  N2: パーツ1.A5, W2.IO5
  N3: パーツ1.RAW, W2.VOUT
  N4: パーツ1.GND, W2.GND#12
  N5: パーツ1.MOSI, J2.pulse
  N6: パーツ1.D10, J1.pulse
  N7: パーツ1.D9, パーツ7.ENABLE
  N8: パーツ1.D8, パーツ7.PHASE
  N9: パーツ1.D7, パーツ6.PHASE
  N10: パーツ1.D6, パーツ6.ENABLE
  N11: パーツ1.D5, パーツ5.ENABLE
  N12: パーツ1.D4, パーツ5.PHASE
  N13: パーツ1.D3, パーツ4.ENABLE
  N14: パーツ1.D2, パーツ4.PHASE
  N15: M1.pin_1, パーツ7.OUT2
  N16: M1.pin_2, パーツ7.OUT1
  N17: M2.pin_1, パーツ6.OUT2
  N18: M2.pin_2, パーツ6.OUT1
  N19: M3.pin_1, パーツ5.OUT2
  N20: M3.pin_2, パーツ5.OUT1
  N21: M4.pin_1, パーツ4.OUT2
  N22: M4.pin_2, パーツ4.OUT1
  GND: J1.gnd, J2.gnd, BAT1.-, U1.GND, パーツ4.GND#0, パーツ5.GND#0, パーツ6.GND#0, パーツ7.GND#0
  VCC: J1.vcc, J2.vcc, U1.input_voltage
  N23: BAT1.+, BAT2.-
  N24: BAT2.+, BAT3.-
  N25: BAT4.+, BAT5.-
  N26: BAT4.-, BAT3.+
  VIN: BAT5.+, U1.output_voltage, パーツ4.VIN, パーツ5.VIN, パーツ6.VIN, パーツ7.VIN
  N27: W2.GND#9, VCC1.-, パーツ4.GND#5, パーツ5.GND#5, パーツ6.GND#5, パーツ7.GND#5
  VCC_2: W2.VIN, VCC1.+, パーツ4.VCC, パーツ5.VCC, パーツ6.VCC, パーツ7.VCC
